# Fritzing sketch arduino-lowpower (saved by Fritzing 0.9.0b)
circuit board: 8.46667cm x 5.64444cm
breadboards: 1

parts:
  U1 = atmega328 [package=dip]
  R1 = Resistor [tolerance=±5% resistance=220 package=THT]
  R2 = Photocell (LDR) [package=THT]
  U3 = LIPO-110mAh [package=lipo-110]
  LED1 = LEDs [package=led10mm]
  NRF24L1 = NRF24L01

nets:
  N1: U1.D4, U1.GND#7, U3.-, LED1.A, LED1.C
  N2: U1.VCC, U3.+
  N3: U1.D9_(PWM), NRF24L1.CSN
  N4: U1.D10_(PWM), NRF24L1.CE
  N5: U1.D11_(PWM), NRF24L1.MOSI
  N6: U1.D12, NRF24L1.IRQ
  N7: U1.D13, NRF24L1.SCK
  N8: U1.AVCC, R1.Pin_1, NRF24L1.VCC
  N9: U1.GND#21, R2.pin_1, NRF24L1.GND
  N10: U1.A0, R1.Pin_0, R2.pin_0

custom parts:
  NRF24L01: NRF24L01 module
