# Fritzing sketch arduino_lowpower (saved by Fritzing 0.9.0b)
circuit board: 8.46667cm x 5.64444cm
breadboards: 1

parts:
  NRF24L1 = NRF24L01
  U3 = LIPO-110mAh [package=lipo-110]
  R1 = Resistor [tolerance=±5% resistance=10k package=THT]
  LED1 = LEDs [package=led10mm]
  R2 = Photocell (LDR) [package=THT]
  U1 = atmega328 [package=dip]
  Q1 = TRANSISTOR_NPN [package=to-92]

nets:
  N1: NRF24L1.VCC, R1.Pin_1, Q1.E
  N2: NRF24L1.CSN, U1.D9_(PWM)
  N3: NRF24L1.MOSI, U1.D11_(PWM)
  N4: NRF24L1.IRQ, U1.D12
  N5: NRF24L1.GND, R2.pin_1, U1.GND#21
  N6: NRF24L1.CE, U1.D10_(PWM)
  N7: NRF24L1.SCK, U1.D13
  N8: U3.+, U1.VCC, Q1.C
  N9: U3.-, LED1.A, LED1.C, U1.D4, U1.GND#7
  N10: R1.Pin_0, R2.pin_0, U1.A0
  N11: U1.D8, Q1.B

custom parts:
  NRF24L01: NRF24L01 module
